# Fritzing sketch YiMultiRemote (saved by Fritzing 0.9.3b)
breadboards: 1

parts:
  WeMos_D1_Mini1 = WeMos D1 Mini
  S1 = Round Pushbutton
  LED1 = LED - 3mm [color="Blue (430nm)" package="3 mm [THT]"]
  5V = Power plug
  J1 = Piezo Speaker

nets:
  N1: WeMos_D1_Mini1.3V3, LED1.anode
  5V: WeMos_D1_Mini1.5V, 5V.VCC
  N2: WeMos_D1_Mini1.D5, J1.pin2
  N3: WeMos_D1_Mini1.D6, LED1.cathode
  N4: WeMos_D1_Mini1.D7, S1.leg0
  N5: WeMos_D1_Mini1.G, S1.leg1, 5V.GND, J1.pin1
